# Fritzing sketch fotoresistor (saved by Fritzing 0.8.5b)
breadboards: 1

parts:
  Raspberry_Pi_B_rev1 = Raspberry Pi B rev2
  R1 = PHOTOCELL [package=photocell]
  C1 = Electrolytic Capacitor [capacitance=1µF package="100 mil [THT, electrolytic]"]
  LED1 = LED - 5mm [color="Green (570nm)" package="5 mm [THT]"]
  LED2 = LED - 5mm [color="Red (633nm)" package="5 mm [THT]"]
  LED3 = LED - 5mm [color="Yellow (595nm)" package="5 mm [THT]"]
  R2 = Resistor [tolerance=±5% resistance=470 package=THT]
  R3 = Resistor [tolerance=±5% resistance=470 package=THT]
  R4 = Resistor [tolerance=±5% resistance=470 package=THT]

nets:
  N1: Raspberry_Pi_B_rev1.3V3, R1.P$2
  N2: Raspberry_Pi_B_rev1.GPIO_3, C1.+, R2.Pin_1, R3.Pin_1, R4.Pin_1
  N3: Raspberry_Pi_B_rev1.GPIO_17, LED3.cathode
  N4: Raspberry_Pi_B_rev1.GPIO_27, LED2.cathode
  N5: Raspberry_Pi_B_rev1.GPIO_22, LED1.cathode
  N6: Raspberry_Pi_B_rev1.GPIO_4, R1.P$1, C1.-
  N7: LED1.anode, R2.Pin_0
  N8: LED2.anode, R3.Pin_0
  N9: LED3.anode, R4.Pin_0
