# Fritzing sketch PWM_Interrupt_Multithreading (saved by Fritzing 0.9.2b)
breadboards: 1

parts:
  Raspberry_Pi_B_rev1 = Raspberry Pi B rev1
  R1 = Resistor [tolerance=±5% resistance=10k package=THT]
  LED1 = LED - 5mm [color="Green (555nm)" package="5 mm [THT]"]
  LED2 = LED - 5mm [color="Yellow (592nm)" package="5 mm [THT]"]
  LED3 = LED - 5mm [color="Red (633nm)" package="5 mm [THT]"]
  R2 = Resistor [tolerance=±5% resistance=220 package=THT]
  R3 = Resistor [tolerance=±5% resistance=220 package=THT]
  R4 = Resistor [tolerance=±5% resistance=220 package=THT]
  S1 = Momentary Switch [package=ksa_sealed_tac_switch]

nets:
  N1: Raspberry_Pi_B_rev1.5V, R1.Pin_1
  N2: Raspberry_Pi_B_rev1.GND, R2.Pin_0, R3.Pin_0, R4.Pin_0, S1.1, S1.3
  N3: Raspberry_Pi_B_rev1.GPIO_17, R1.Pin_0, S1.2, S1.4
  N4: Raspberry_Pi_B_rev1.GPIO_18, LED3.anode
  N5: Raspberry_Pi_B_rev1.GPIO_21, LED2.anode
  N6: LED1.cathode, LED1.anode, R2.Pin_1
  N7: LED2.cathode, R3.Pin_1
  N8: LED3.cathode, R4.Pin_1
