# Fritzing sketch PWM_Interrupt_Multithreading_NoPhisicalBtn (saved by Fritzing 0.9.2b)
breadboards: 1

parts:
  Raspberry_Pi_B_rev1 = Raspberry Pi B rev1
  LED1 = LED - 5mm [color="Green (555nm)" package="5 mm [THT]"]
  LED2 = LED - 5mm [color="Yellow (592nm)" package="5 mm [THT]"]
  LED3 = LED - 5mm [color="Red (633nm)" package="5 mm [THT]"]
  R2 = Resistor [tolerance=±5% resistance=220 package=THT]
  R3 = Resistor [tolerance=±5% resistance=220 package=THT]
  R4 = Resistor [tolerance=±5% resistance=220 package=THT]

nets:
  N1: Raspberry_Pi_B_rev1.GND, R2.Pin_0, R3.Pin_0, R4.Pin_0
  N2: Raspberry_Pi_B_rev1.GPIO_23, Raspberry_Pi_B_rev1.GPIO_17
  N3: Raspberry_Pi_B_rev1.GPIO_18, LED3.anode
  N4: Raspberry_Pi_B_rev1.GPIO_21, LED2.anode
  N5: LED1.cathode, LED1.anode, R2.Pin_1
  N6: LED2.cathode, R3.Pin_1
  N7: LED3.cathode, R4.Pin_1
